# Fritzing sketch Semaforo (saved by Fritzing 0.9.3b)
breadboards: 1

parts:
  Componente1 = Arduino Uno (Rev3)
  LED1 = LED - 5mm [color="Green (570nm)" package="5 mm [THT]"]
  LED2 = LED - 5mm [color="Yellow (595nm)" package="5 mm [THT]"]
  LED3 = LED - 5mm [color="Red (633nm)" package="5 mm [THT]"]
  LED4 = LED - 5mm [color="Red (633nm)" package="5 mm [THT]"]
  LED5 = LED - 5mm [color="Green (570nm)" package="5 mm [THT]"]
  R1 = Resistor [tolerance=±5% resistance=220 package=THT]
  R2 = Resistor [tolerance=±5% resistance=220 package=THT]
  R4 = Resistor [tolerance=±5% resistance=220 package=THT]
  R5 = Resistor [tolerance=±5% resistance=220 package=THT]
  S1 = Pushbutton [package="[THT]"]
  R6 = Resistor [tolerance=±5% resistance=220 package=THT]
  U1 = POT [package=pot_mammoth]

nets:
  N1: Componente1.A0, U1.A
  N2: Componente1.D8, S1.Pin_3, S1.Pin_4
  N3: Componente1.D9_PWM, R1.Pin_1
  N4: Componente1.D10_PWM/SS, R2.Pin_1
  N5: Componente1.D11_PWM/MOSI, R6.Pin_1
  N6: Componente1.D12/MISO, R4.Pin_1
  N7: Componente1.D13/SCK, R5.Pin_1
  N8: Componente1.5V, U1.E
  N9: Componente1.GND, LED1.anode, LED2.anode, LED3.anode, LED4.anode, LED5.anode, S1.Pin_1, S1.Pin_2, U1.S
  N10: LED1.cathode, R1.Pin_0
  N11: LED2.cathode, R2.Pin_0
  N12: LED3.cathode, R6.Pin_0
  N13: LED5.cathode, R5.Pin_0
